// Logisim project RISCV.circ as structural Verilog: 6 circuits, main circuit RISCV
module Inc4 (
  input  [31:0] A,
  output [31:0] S
);

  // Incrementer #(.width(30)) incrementer_1: pin names not known; wires that end beside it: A[31:2], S[31:2]

  assign S[1:0] = A[1:0];
endmodule

module SelectALUOpcode (
  input  b30,
  input  b13,
  input  b12,
  input  b11,
  input  b5,
  input  b4,
  output Op0,
  output Op1,
  output Op2,
  output Op3
);

  wire and_1_out, and_2_out, and_3_out, and_4_out;

  and and_1 (and_1_out, b12, b4);
  and and_2 (and_2_out, b30, b4, b5);
  and and_3 (and_3_out, b13, ~b30);  // AND_Gate
  and and_4 (and_4_out, b13, ~b5);  // AND_Gate
  or or_1 (Op1, b11, and_1_out);
  or or_2 (Op2, b13, and_2_out);
  or or_3 (Op3, and_3_out, and_4_out);

  assign Op0 = b11;
endmodule

module getSelectorBits (
  input  b1,
  input  b0,
  output s3,
  output s2,
  output s1,
  output s0
);

  wire not_1_out, not_2_out, not_3_out, not_4_out;

  and and_1 (s3, b1, b0);
  not not_1 (not_1_out, b0);
  not not_2 (not_2_out, b1);
  not not_3 (not_3_out, b1);
  not not_4 (not_4_out, b0);
  and and_2 (s2, b1, not_1_out);
  and and_3 (s1, not_2_out, b0);
  and and_4 (s0, not_3_out, not_4_out);
endmodule

module selectOutputByte (
  input  [31:0] D,
  input  [1:0] n,
  output [31:0] out_3
);

  wire [31:0] bit_extender_1_out, bit_extender_2_out, bit_extender_3_out, bit_extender_4_out;

  assign bit_extender_1_out = {{24{1'b0}}, D[31:24]};  // Bit_Extender bit_extender_1
  assign bit_extender_2_out = {{24{1'b0}}, D[23:16]};  // Bit_Extender bit_extender_2
  assign bit_extender_3_out = {{24{1'b0}}, D[15:8]};  // Bit_Extender bit_extender_3
  assign bit_extender_4_out = {{24{1'b0}}, D[7:0]};  // Bit_Extender bit_extender_4
  Multiplexer #(.select(2), .width(32), .enable("false")) multiplexer_1 (
    .in0(bit_extender_1_out), .in1(bit_extender_2_out), .in2(bit_extender_3_out), .in3(bit_extender_4_out),
    .out(out_3), .sel(n));
endmodule

module selectInputByte (
  input  [31:0] D,
  input  [1:0] n,
  output [31:0] out_3
);

  Multiplexer #(.select(2), .width(32), .enable("false")) multiplexer_1 (
    .in0({D[7:0], {24{1'b0}}}), .in1({{8{1'b0}}, D[7:0], {16{1'b0}}}), .in2({{16{1'b0}}, D[7:0], {8{1'b0}}}),
    .in3({{24{1'b0}}, D[7:0]}), .out(out_3), .sel(n));
endmodule

module RISCV (
);

  wire and_1_out, and_2_out, clock_1_out, comparator_black_box_1_p4, nand_1_out, not_1_out, registerfile_1_p7;
  wire [3:0] getselectorbits_1_s3, multiplexer_3_out, selectaluopcode_1_op0;
  wire [11:0] multiplexer_1_out, risc_vprogramrom_1_p2;
  wire [31:0] alu_1_p2, alu_1_p5, bit_extender_1_out, bit_extender_2_out, inc4_1_s, multiplexer_4_out,
       multiplexer_5_out, multiplexer_6_out, multiplexer_7_out, ram_1_p7, register_1_q, registerfile_1_p1,
       registerfile_1_p8, selectinputbyte_1_out_3, selectoutputbyte_1_out_3;
  wire [31:12] risc_vprogramrom_1_p2_2;

  Clock clock_1 (.out(clock_1_out));
  Register #(.width(32)) register_1 (.D(inc4_1_s), .clk(clock_1_out), .Q(register_1_q));  // open: en, clr
  Inc4 inc4_1 (.A(register_1_q), .S(inc4_1_s));
  // RISC_VProgramROM risc_vprogramrom_1: pin names not known; wires that end beside it: register_1_q, {risc_vprogramrom_1_p2_2, risc_vprogramrom_1_p2}
  Multiplexer #(.width(12), .enable("false")) multiplexer_1 (
    .in0({risc_vprogramrom_1_p2_2[31:25], risc_vprogramrom_1_p2[11:7]}),
    .in1(risc_vprogramrom_1_p2_2[31:20]), .out(multiplexer_1_out), .sel(nand_1_out));
  nand nand_1 (nand_1_out, risc_vprogramrom_1_p2[5], ~risc_vprogramrom_1_p2[4]);  // NAND_Gate
  and and_1 (and_1_out, risc_vprogramrom_1_p2[5], risc_vprogramrom_1_p2[4]);
  assign bit_extender_1_out = {{20{multiplexer_1_out[11]}}, multiplexer_1_out};  // Bit_Extender bit_extender_1
  // RegisterFile registerfile_1: pin names not known; wires that end beside it: registerfile_1_p1, clock_1_out, nand_1_out, risc_vprogramrom_1_p2[11:7], risc_vprogramrom_1_p2_2[19:15], risc_vprogramrom_1_p2_2[24:20], registerfile_1_p7, registerfile_1_p8
  SelectALUOpcode selectaluopcode_1 (
    .b30(risc_vprogramrom_1_p2_2[30]), .b13(risc_vprogramrom_1_p2_2[14]), .b12(risc_vprogramrom_1_p2_2[13]),
    .b11(risc_vprogramrom_1_p2_2[12]), .b5(risc_vprogramrom_1_p2[5]), .b4(risc_vprogramrom_1_p2[4]),
    .Op0(selectaluopcode_1_op0[0]), .Op1(selectaluopcode_1_op0[1]), .Op2(selectaluopcode_1_op0[2]),
    .Op3(selectaluopcode_1_op0[3]));
  // ALU alu_1: pin names not known; wires that end beside it: registerfile_1_p7, alu_1_p2, selectaluopcode_1_op0, registerfile_1_p8[4:0], alu_1_p5
  Multiplexer #(.width(32), .enable("false")) multiplexer_2 (
    .in0(bit_extender_1_out), .in1(registerfile_1_p8), .out(alu_1_p2), .sel(and_1_out));
  // Comparator_Black_Box comparator_black_box_1: pin names not known; wires that end beside it: registerfile_1_p7, alu_1_p2, 1'b1, comparator_black_box_1_p4
  not not_1 (not_1_out, nand_1_out);
  assign bit_extender_2_out = {{31{1'b0}}, comparator_black_box_1_p4};  // Bit_Extender bit_extender_2
  Multiplexer #(.width(4), .enable("false")) multiplexer_3 (
    .in0(getselectorbits_1_s3), .in1(4'b1111), .out(multiplexer_3_out), .sel(risc_vprogramrom_1_p2_2[13]));
  getSelectorBits getselectorbits_1 (
    .b1(alu_1_p5[1]), .b0(alu_1_p5[0]), .s3(getselectorbits_1_s3[0]), .s2(getselectorbits_1_s3[1]),
    .s1(getselectorbits_1_s3[2]), .s0(getselectorbits_1_s3[3]));
  selectInputByte selectinputbyte_1 (.D(registerfile_1_p8), .n(alu_1_p5[1:0]), .out_3(selectinputbyte_1_out_3));
  Multiplexer #(.width(32), .enable("false")) multiplexer_4 (
    .in0(selectinputbyte_1_out_3), .in1(registerfile_1_p8), .out(multiplexer_4_out),
    .sel(risc_vprogramrom_1_p2_2[13]));
  and and_2 (and_2_out, ~risc_vprogramrom_1_p2_2[14], risc_vprogramrom_1_p2_2[13], ~risc_vprogramrom_1_p2_2[12]);  // AND_Gate
  Multiplexer #(.width(32), .enable("false")) multiplexer_5 (
    .in0(alu_1_p5), .in1(bit_extender_2_out), .out(multiplexer_5_out), .sel(and_2_out));
  // RAM ram_1: pin names not known; wires that end beside it: alu_1_p5[21:2], multiplexer_4_out, not_1_out, multiplexer_3_out, clock_1_out, nand_1_out, ram_1_p7
  selectOutputByte selectoutputbyte_1 (.D(ram_1_p7), .n(alu_1_p5[1:0]), .out_3(selectoutputbyte_1_out_3));
  Multiplexer #(.width(32), .enable("false")) multiplexer_6 (
    .in0(selectoutputbyte_1_out_3), .in1(ram_1_p7), .out(multiplexer_6_out), .sel(risc_vprogramrom_1_p2_2[13]));
  Multiplexer #(.width(32), .enable("false")) multiplexer_7 (
    .in0(multiplexer_6_out), .in1(multiplexer_5_out), .out(multiplexer_7_out), .sel(risc_vprogramrom_1_p2[4]));
  Multiplexer #(.width(32), .enable("false")) multiplexer_8 (
    .in0(multiplexer_7_out), .in1({risc_vprogramrom_1_p2_2, {12{1'b0}}}), .out(registerfile_1_p1),
    .sel(risc_vprogramrom_1_p2[2]));

  // Notes on the sheet:
  //   contents of risc_vprogramrom_1 (hex, n*v repeats v):
  //   # testing 0 sub 0 == 0 addi x1, x0, 0 addi x2, x0, 0 sub x3, x1, x2 ## expect[3] = 0 # testing 0 sub
  //   -1 == 1 addi x1, x0, 0 addi x2, x0, -1 sub x4, x1, x2 ## expect[4] = 1 # testing 0 sub 2147483647 ==
  //   -2147483647 addi x1, x0, 0 lui x2, 524287 addi x2, x2, -1 sub x5, x1, x2 ## expect[5] = -2147483647
  //   # testing 0 sub -2147483648 == -2147483648 addi x1, x0, 0 lui x2, -524288 addi x2, x2, 0 sub x6, x1,
  //   x2 ## expect[6] = -2147483648 # testing -1 sub 0 == -1 addi x1, x0, -1 addi x2, x0, 0 sub x7, x1, x2
  //   ## expect[7] = -1 # testing -1 sub -1 == 0 addi x1, x0, -1 addi x2, x0, -1 sub x8, x1, x2 ##
  //   expect[8] = 0 # testing -1 sub 2147483647 == -2147483648 addi x1, x0, -1 lui x2, 524287 addi x2, x2,
  //   -1 sub x9, x1, x2 ## expect[9] = -2147483648 # testing -1 sub -2147483648 == 2147483647 addi x1, x0,
  //   -1 lui x2, -524288 addi x2, x2, 0 sub x10, x1, x2 ## expect[10] = 2147483647 # testing 2147483647
  //   sub 0 == 2147483647 lui x1, 524287 addi x1, x1, -1 addi x2, x0, 0 sub x11, x1, x2 ## expect[11] =
  //   2147483647 # testing 2147483647 sub -1 == -2147483648 lui x1, 524287 addi x1, x1, -1 addi x2, x0, -1
  //   sub x12, x1, x2 ## expect[12] = -2147483648 # testing 2147483647 sub 2147483647 == 0 lui x1, 524287
  //   addi x1, x1, -1 lui x2, 524287 addi x2, x2, -1 sub x13, x1, x2 ## expect[13] = 0 # testing
  //   2147483647 sub -2147483648 == -1 lui x1, 524287 addi x1, x1, -1 lui x2, -524288 addi x2, x2, 0 sub
  //   x14, x1, x2 ## expect[14] = -1 # testing -2147483648 sub 0 == -2147483648 lui x1, -524288 addi x1,
  //   x1, 0 addi x2, x0, 0 sub x15, x1, x2 ## expect[15] = -2147483648 # testing -2147483648 sub -1 ==
  //   -2147483647 lui x1, -524288 addi x1, x1, 0 addi x2, x0, -1 sub x16, x1, x2 ## expect[16] =
  //   -2147483647 # testing -2147483648 sub 2147483647 == 1 lui x1, -524288 addi x1, x1, 0 lui x2, 524287
  //   addi x2, x2, -1 sub x17, x1, x2 ## expect[17] = 1 # testing -2147483648 sub -2147483648 == 0 lui x1,
  //   -524288 addi x1, x1, 0 lui x2, -524288 addi x2, x2, 0 sub x18, x1, x2 ## expect[18] = 0 addi x1, x0,
  //   0 addi x2, x0, 0 ## cycles = 64
endmodule
